# Fritzing sketch ArtNet Node (saved by Fritzing 0.9.2b)
circuit board: 8.35857cm x 5.46029cm
breadboards: 1

parts:
  Part1 = Arduino Mega 2560 (Rev3)
  R6 = Resistor [tolerance=±5% resistance=100 package=THT]
  R7 = Resistor [tolerance=±5% resistance=100 package=THT]
  R8 = Resistor [tolerance=±5% resistance=100 package=THT]
  LED_Conn = screw terminal, 4 pins
  B_channel1 = MAX485 [package=dil08]
  J5 = screw terminal, 3 pins
  A_channel1 = MAX485 [package=dil08]
  J6 = screw terminal, 3 pins
  U2 = mystery part, 4 pins [chip_label=?]
  R9 = Resistor [tolerance=±5% resistance=10k package=THT]
  R10 = Resistor [tolerance=±5% resistance=10k package=THT]
  LCD_Conn = screw terminal, 4 pins

nets:
  N1: Part1.A8, U2.pin1, R9.Pin_1
  N2: Part1.A9, U2.pin3, R10.Pin_1
  N3: Part1.D21/SCL, LCD_Conn.pin4
  N4: Part1.D20/SDA, LCD_Conn.pin3
  N5: Part1.D19/RX1, B_channel1.RO
  N6: Part1.D18/TX1, B_channel1.DI
  GND: Part1.GND, B_channel1.GND, J5.pin1, A_channel1.GND, J6.pin1, R9.Pin_0, R10.Pin_0, LCD_Conn.pin2
  N7: Part1.D12_PWM, R8.Pin_1
  N8: Part1.D11_PWM, R7.Pin_1
  N9: Part1.D9_PWM, R6.Pin_1
  VCC: Part1.5V, LED_Conn.pin1, B_channel1.VCC, A_channel1.VCC, U2.pin2, U2.pin4, LCD_Conn.pin1
  N10: Part1.D0_RX0, A_channel1.RO
  N11: Part1.D1_TX0, A_channel1.DI
  N12: Part1.D2_PWM, A_channel1.RE, A_channel1.DE
  N13: Part1.D3_PWM, B_channel1.RE, B_channel1.DE
  N14: R6.Pin_0, LED_Conn.pin2
  N15: R7.Pin_0, LED_Conn.pin3
  N16: R8.Pin_0, LED_Conn.pin4
  N17: B_channel1.A, J5.pin2
  N18: B_channel1.B, J5.pin3
  N19: A_channel1.A, J6.pin2
  N20: A_channel1.B, J6.pin3

notes:
  LED Connectors
  LCD Connector
  Unknown
